// Logisim project BiggerComputer.circ as structural Verilog: 11 circuits, main circuit main
module main (
  output [15:0] Core0,
  output [15:0] out_2,
  output [63:0] out_3,
  output [15:0] out_4,
  output [63:0] out_5,
  output [15:0] out_6,
  output [15:0] out_7,
  output [63:0] out_8,
  output [15:0] out_9,
  output [15:0] out_10,
  output [63:0] out_11,
  output [15:0] Overflow0,
  output [15:0] Core1,
  output [15:0] out_14,
  output [15:0] out_15,
  output [15:0] out_16,
  output [15:0] out_17,
  output [15:0] out_18,
  output [15:0] out_19,
  output [15:0] Overflow1,
  output [15:0] Core2,
  output [15:0] out_22,
  output [15:0] out_23,
  output [15:0] out_24,
  output [15:0] out_25,
  output [15:0] out_26,
  output [15:0] out_27,
  output [15:0] Overflow2,
  output [15:0] Core3,
  output [15:0] out_30,
  output [15:0] out_31,
  output [15:0] out_32,
  output [15:0] out_33,
  output [15:0] out_34,
  output [15:0] out_35,
  output [15:0] Overflow3
);

  wire clock_1_out, clock_2_out, clock_3_out, clock_4_out, clock_5_out, clock_6_out, clock_7_out,
       clock_8_out, comparator_1_eq, comparator_2_eq, comparator_3_eq, comparator_4_eq, comparator_5_eq,
       comparator_6_eq, comparator_7_eq, comparator_8_eq, comparator_9_eq, comparator_10_eq,
       core_1_write_enable, core_2_write_enable, core_3_write_enable, core_4_write_enable,
       demultiplexer_2_out0, demultiplexer_2_out1, demultiplexer_2_out2, demultiplexer_2_out3,
       demultiplexer_5_out0, demultiplexer_5_out1, demultiplexer_5_out2, demultiplexer_5_out3,
       demultiplexer_8_out0, demultiplexer_8_out1, demultiplexer_8_out2, demultiplexer_8_out3,
       demultiplexer_11_out0, demultiplexer_11_out1, demultiplexer_11_out2, demultiplexer_11_out3,
       store_check_1_mem_0_write, store_check_1_mem_1_write, store_check_1_mem_2_write,
       store_check_1_mem_3_write, store_check_2_mem_0_write, store_check_2_mem_1_write,
       store_check_2_mem_2_write, store_check_2_mem_3_write, store_check_3_mem_0_write,
       store_check_3_mem_1_write, store_check_3_mem_2_write, store_check_3_mem_3_write,
       store_check_4_mem_0_write, store_check_4_mem_1_write, store_check_4_mem_2_write,
       store_check_4_mem_3_write, xor_1_out, xor_2_out, xor_3_out, xor_4_out;
  wire [1:0] bitselector_2_out, bitselector_4_out, bitselector_6_out, bitselector_8_out;
  wire [5:0] bitselector_1_out, bitselector_3_out, bitselector_5_out, bitselector_7_out, bitselector_9_out,
       demultiplexer_1_out0;
  wire [7:0] controlled_buffer_1_out, controlled_buffer_2_out, controlled_buffer_3_out,
       controlled_buffer_4_out, counter_1_q;
  wire [15:0] core_1_data_out, core_1_overflow_out, core_2_data_out, core_2_overflow_out, core_3_data_out,
       core_3_overflow_out, core_4_data_out, core_4_overflow_out, counters_1_down_counter,
       counters_1_up_counter, demultiplexer_3_out0, demultiplexer_3_out1, demultiplexer_3_out2,
       demultiplexer_3_out3, multiplexer_1_out, multiplexer_2_out, multiplexer_3_out, multiplexer_4_out,
       RAM_0, RAM_1, RAM_2, RAM_3, registers_1_ri_out_0, registers_1_ri_out_1, registers_1_ri_out_2,
       registers_1_ri_out_3, registers_1_rj_out_0, registers_1_rj_out_1, registers_1_rj_out_2,
       registers_1_rj_out_3;
  wire [31:0] ROM_0, ROM_1, ROM_2, ROM_3;
  wire [63:0] vector_unit_1_vi_out, vector_unit_1_vj_out;

  Counter #(.trigger("falling")) counter_1 (
    .load(comparator_1_eq), .up(1'b1), .clk(clock_1_out), .D(ROM_0[15:8]), .Q(counter_1_q));  // open: clr, count, carry
  Clock clock_1 (.out(clock_1_out));
  ROM #(.dataWidth(32)) CORE_0_ROM (.addr(counter_1_q), .data(ROM_0));
  ROM #(.dataWidth(32)) CORE_1_ROM (.addr(counter_1_q), .data(ROM_1));
  ROM #(.dataWidth(32)) CORE_2_ROM (.addr(counter_1_q), .data(ROM_2));
  ROM #(.dataWidth(32)) CORE_3_ROM (.addr(counter_1_q), .data(ROM_3));
  Comparator comparator_1 (.a({8{1'b1}}), .b(ROM_0[31:24]), .eq(comparator_1_eq));  // open: gt, lt
  Clock clock_2 (.out(clock_2_out));
  Registers registers_1 (
    .OVERFLOW_0(core_1_overflow_out), .WRITE_ENABLE_1(core_2_write_enable),
    .WRITE_ENABLE_2(core_3_write_enable), .WRITE_ENABLE_3(core_4_write_enable), .Rk_DEMUX_1(ROM_1[7:0]),
    .DATA_IN_1(multiplexer_2_out), .Rk_DEMUX_2(ROM_2[7:0]), .DATA_IN_2(multiplexer_3_out),
    .Rk_DEMUX_3(ROM_3[7:0]), .DATA_IN_3(multiplexer_4_out), .Rj_MUX_0(ROM_0[15:8]), .Rj_MUX_1(ROM_1[15:8]),
    .Rj_MUX_2(ROM_2[15:8]), .Rj_MUX_3(ROM_3[15:8]), .Ri_MUX_0(ROM_0[23:16]), .Ri_MUX_1(ROM_1[23:16]),
    .Ri_MUX_2(ROM_2[23:16]), .WRITE_ENABLE_0(core_1_write_enable), .DATA_IN_0(multiplexer_1_out),
    .OVERFLOW_1(core_2_overflow_out), .Rk_DEMUX_0(ROM_0[7:0]), .Ri_MUX_3(ROM_3[23:16]),
    .OVERFLOW_2(core_3_overflow_out), .OVERFLOW_3(core_4_overflow_out), .CLOCK(clock_2_out),
    .Rj_OUT_0(registers_1_rj_out_0), .Rj_OUT_1(registers_1_rj_out_1), .Rj_OUT_2(registers_1_rj_out_2),
    .Rj_OUT_3(registers_1_rj_out_3), .Ri_OUT_0(registers_1_ri_out_0), .Ri_OUT_1(registers_1_ri_out_1),
    .Ri_OUT_2(registers_1_ri_out_2), .A0(Core0), .A1(out_2), .A2(out_4), .A3(out_6), .A4(out_7), .A5(out_9),
    .A6(out_10), .A7(Overflow0), .A8(Core1), .A9(out_14), .AA(out_15), .AB(out_16), .AC(out_17), .AD(out_18),
    .AE(out_19), .AF(Overflow1), .Ri_OUT_3(registers_1_ri_out_3), .B0(Core2), .B1(out_22), .B2(out_23),
    .B3(out_24), .B4(out_25), .B5(out_26), .B6(out_27), .B7(Overflow2), .B8(Core3), .B9(out_30), .BA(out_31),
    .BB(out_32), .BC(out_33), .BD(out_34), .BE(out_35), .BF(Overflow3));
  Clock clock_3 (.out(clock_3_out));
  Counters counters_1 (.CLOCK(clock_3_out), .UP_COUNTER(counters_1_up_counter), .DOWN_COUNTER(counters_1_down_counter));
  CORE core_1 (
    .UP_COUNTER(counters_1_up_counter), .DOWN_COUNTER(counters_1_down_counter), .Ri(registers_1_ri_out_0),
    .Rj(registers_1_rj_out_0), .OPCODE(ROM_0[31:24]), .OVERFLOW_OUT(core_1_overflow_out),
    .DATA_OUT(core_1_data_out), .WRITE_ENABLE(core_1_write_enable));
  CORE core_2 (
    .UP_COUNTER(counters_1_up_counter), .DOWN_COUNTER(counters_1_down_counter), .Ri(registers_1_ri_out_1),
    .Rj(registers_1_rj_out_1), .OPCODE(ROM_1[31:24]), .OVERFLOW_OUT(core_2_overflow_out),
    .DATA_OUT(core_2_data_out), .WRITE_ENABLE(core_2_write_enable));
  CORE core_3 (
    .UP_COUNTER(counters_1_up_counter), .DOWN_COUNTER(counters_1_down_counter), .Ri(registers_1_ri_out_2),
    .Rj(registers_1_rj_out_2), .OPCODE(ROM_2[31:24]), .OVERFLOW_OUT(core_3_overflow_out),
    .DATA_OUT(core_3_data_out), .WRITE_ENABLE(core_3_write_enable));
  CORE core_4 (
    .UP_COUNTER(counters_1_up_counter), .DOWN_COUNTER(counters_1_down_counter), .Ri(registers_1_ri_out_3),
    .Rj(registers_1_rj_out_3), .OPCODE(ROM_3[31:24]), .OVERFLOW_OUT(core_4_overflow_out),
    .DATA_OUT(core_4_data_out), .WRITE_ENABLE(core_4_write_enable));
  Multiplexer #(.width(16)) multiplexer_1 (
    .in0(core_1_data_out), .in1(RAM_0), .out(multiplexer_1_out), .sel(comparator_2_eq));
  Multiplexer #(.width(16)) multiplexer_2 (
    .in0(core_2_data_out), .in1(RAM_1), .out(multiplexer_2_out), .sel(comparator_3_eq));
  Multiplexer #(.width(16)) multiplexer_3 (
    .in0(core_3_data_out), .in1(RAM_2), .out(multiplexer_3_out), .sel(comparator_4_eq));
  Multiplexer #(.width(16)) multiplexer_4 (
    .in0(core_4_data_out), .in1(RAM_3), .out(multiplexer_4_out), .sel(comparator_5_eq));
  Comparator comparator_2 (.a(ROM_0[31:24]), .b(8'h40), .eq(comparator_2_eq));  // open: gt, lt
  Comparator comparator_3 (.a(ROM_1[31:24]), .b(8'h40), .eq(comparator_3_eq));  // open: gt, lt
  Comparator comparator_4 (.a(ROM_2[31:24]), .b(8'h40), .eq(comparator_4_eq));  // open: gt, lt
  Comparator comparator_5 (.a(ROM_3[31:24]), .b(8'h40), .eq(comparator_5_eq));  // open: gt, lt
  assign controlled_buffer_1_out = comparator_6_eq ? ROM_0[7:0] : 8'bz;  // Controlled_Buffer controlled_buffer_1
  Comparator comparator_6 (.a(ROM_0[31:24]), .b(8'h41), .eq(comparator_6_eq));  // open: gt, lt
  assign controlled_buffer_2_out = comparator_7_eq ? ROM_1[7:0] : 8'bz;  // Controlled_Buffer controlled_buffer_2
  Comparator comparator_7 (.a(ROM_1[31:24]), .b(8'h41), .eq(comparator_7_eq));  // open: gt, lt
  assign controlled_buffer_3_out = comparator_8_eq ? ROM_2[7:0] : 8'bz;  // Controlled_Buffer controlled_buffer_3
  Comparator comparator_8 (.a(ROM_2[31:24]), .b(8'h41), .eq(comparator_8_eq));  // open: gt, lt
  assign controlled_buffer_4_out = comparator_9_eq ? ROM_3[7:0] : 8'bz;  // Controlled_Buffer controlled_buffer_4
  Comparator comparator_9 (.a(ROM_3[31:24]), .b(8'h41), .eq(comparator_9_eq));  // open: gt, lt
  BitSelector #(.group(6)) bitselector_1 (.in(ROM_0[15:8]), .out(bitselector_1_out), .sel(1'b0));
  Demultiplexer #(.disabled("Z"), .select(2), .tristate("true"), .width(6)) demultiplexer_1 (
    .out0(demultiplexer_1_out0), .out1(demultiplexer_1_out0), .out2(demultiplexer_1_out0),
    .out3(demultiplexer_1_out0), .in(bitselector_1_out), .sel(bitselector_2_out));
  BitSelector #(.group(2)) bitselector_2 (.in(controlled_buffer_1_out), .out(bitselector_2_out), .sel(2'b00));
  Demultiplexer #(.disabled("Z"), .select(2), .tristate("true")) demultiplexer_2 (
    .out0(demultiplexer_2_out0), .out1(demultiplexer_2_out1), .out2(demultiplexer_2_out2),
    .out3(demultiplexer_2_out3), .in(1'b1), .sel(bitselector_2_out));
  Demultiplexer #(.disabled("Z"), .select(2), .tristate("true"), .width(16)) demultiplexer_3 (
    .out0(demultiplexer_3_out0), .out1(demultiplexer_3_out1), .out2(demultiplexer_3_out2),
    .out3(demultiplexer_3_out3), .in(registers_1_ri_out_0), .sel(bitselector_2_out));
  BitSelector #(.group(6)) bitselector_3 (.in(ROM_1[15:8]), .out(bitselector_3_out), .sel(1'b0));
  Demultiplexer #(.disabled("Z"), .select(2), .tristate("true"), .width(6)) demultiplexer_4 (
    .out0(demultiplexer_1_out0), .out1(demultiplexer_1_out0), .out2(demultiplexer_1_out0),
    .out3(demultiplexer_1_out0), .in(bitselector_3_out), .sel(bitselector_4_out));
  BitSelector #(.group(2)) bitselector_4 (.in(controlled_buffer_2_out), .out(bitselector_4_out), .sel(2'b00));
  Demultiplexer #(.disabled("Z"), .select(2), .tristate("true")) demultiplexer_5 (
    .out0(demultiplexer_5_out0), .out1(demultiplexer_5_out1), .out2(demultiplexer_5_out2),
    .out3(demultiplexer_5_out3), .in(1'b1), .sel(bitselector_4_out));
  Demultiplexer #(.disabled("Z"), .select(2), .tristate("true"), .width(16)) demultiplexer_6 (
    .out0(demultiplexer_3_out0), .out1(demultiplexer_3_out1), .out2(demultiplexer_3_out2),
    .out3(demultiplexer_3_out3), .in(registers_1_ri_out_1), .sel(bitselector_4_out));
  BitSelector #(.group(6)) bitselector_5 (.in(ROM_2[15:8]), .out(bitselector_5_out), .sel(1'b0));
  Demultiplexer #(.disabled("Z"), .select(2), .tristate("true"), .width(6)) demultiplexer_7 (
    .out0(demultiplexer_1_out0), .out1(demultiplexer_1_out0), .out2(demultiplexer_1_out0),
    .out3(demultiplexer_1_out0), .in(bitselector_5_out), .sel(bitselector_6_out));
  BitSelector #(.group(2)) bitselector_6 (.in(controlled_buffer_3_out), .out(bitselector_6_out), .sel(2'b00));
  Demultiplexer #(.disabled("Z"), .select(2), .tristate("true")) demultiplexer_8 (
    .out0(demultiplexer_8_out0), .out1(demultiplexer_8_out1), .out2(demultiplexer_8_out2),
    .out3(demultiplexer_8_out3), .in(1'b1), .sel(bitselector_6_out));
  Demultiplexer #(.disabled("Z"), .select(2), .tristate("true"), .width(16)) demultiplexer_9 (
    .out0(demultiplexer_3_out0), .out1(demultiplexer_3_out1), .out2(demultiplexer_3_out2),
    .out3(demultiplexer_3_out3), .in(registers_1_ri_out_2), .sel(bitselector_6_out));
  BitSelector #(.group(6)) bitselector_7 (.in(ROM_3[15:8]), .out(bitselector_7_out), .sel(1'b0));
  Demultiplexer #(.disabled("Z"), .select(2), .tristate("true"), .width(6)) demultiplexer_10 (
    .out0(demultiplexer_1_out0), .out1(demultiplexer_1_out0), .out2(demultiplexer_1_out0),
    .out3(demultiplexer_1_out0), .in(bitselector_7_out), .sel(bitselector_8_out));
  BitSelector #(.group(2)) bitselector_8 (.in(controlled_buffer_4_out), .out(bitselector_8_out), .sel(2'b00));
  Demultiplexer #(.disabled("Z"), .select(2), .tristate("true")) demultiplexer_11 (
    .out0(demultiplexer_11_out0), .out1(demultiplexer_11_out1), .out2(demultiplexer_11_out2),
    .out3(demultiplexer_11_out3), .in(1'b1), .sel(bitselector_8_out));
  Demultiplexer #(.disabled("Z"), .select(2), .tristate("true"), .width(16)) demultiplexer_12 (
    .out0(demultiplexer_3_out0), .out1(demultiplexer_3_out1), .out2(demultiplexer_3_out2),
    .out3(demultiplexer_3_out3), .in(registers_1_ri_out_3), .sel(bitselector_8_out));
  Store_Check store_check_1 (
    .ROM_0_CHECK(demultiplexer_2_out0), .OPCODE(ROM_0[31:24]), .ROM_1_CHECK(demultiplexer_2_out1),
    .ROM_2_CHECK(demultiplexer_2_out2), .ROM_3_CHECK(demultiplexer_2_out3),
    .MEM_0_WRITE(store_check_1_mem_0_write), .MEM_1_WRITE(store_check_1_mem_1_write),
    .MEM_2_WRITE(store_check_1_mem_2_write), .MEM_3_WRITE(store_check_1_mem_3_write));
  Store_Check store_check_2 (
    .ROM_0_CHECK(demultiplexer_5_out0), .OPCODE(ROM_1[31:24]), .ROM_1_CHECK(demultiplexer_5_out1),
    .ROM_2_CHECK(demultiplexer_5_out2), .ROM_3_CHECK(demultiplexer_5_out3),
    .MEM_0_WRITE(store_check_2_mem_0_write), .MEM_1_WRITE(store_check_2_mem_1_write),
    .MEM_2_WRITE(store_check_2_mem_2_write), .MEM_3_WRITE(store_check_2_mem_3_write));
  Store_Check store_check_3 (
    .ROM_0_CHECK(demultiplexer_8_out0), .OPCODE(ROM_2[31:24]), .ROM_1_CHECK(demultiplexer_8_out1),
    .ROM_2_CHECK(demultiplexer_8_out2), .ROM_3_CHECK(demultiplexer_8_out3),
    .MEM_0_WRITE(store_check_3_mem_0_write), .MEM_1_WRITE(store_check_3_mem_1_write),
    .MEM_2_WRITE(store_check_3_mem_2_write), .MEM_3_WRITE(store_check_3_mem_3_write));
  Store_Check store_check_4 (
    .ROM_0_CHECK(demultiplexer_11_out0), .OPCODE(ROM_3[31:24]), .ROM_1_CHECK(demultiplexer_11_out1),
    .ROM_2_CHECK(demultiplexer_11_out2), .ROM_3_CHECK(demultiplexer_11_out3),
    .MEM_0_WRITE(store_check_4_mem_0_write), .MEM_1_WRITE(store_check_4_mem_1_write),
    .MEM_2_WRITE(store_check_4_mem_2_write), .MEM_3_WRITE(store_check_4_mem_3_write));
  RAM #(.addrWidth(6), .dataWidth(16)) u_ram_1 (
    .addr(demultiplexer_1_out0), .we(xor_1_out), .oe(1'b1), .clk(clock_4_out), .din(demultiplexer_3_out0),
    .dout(RAM_0));
  ExactlyOne xor_1 (
    .out(xor_1_out), .in0(store_check_1_mem_0_write), .in1(store_check_2_mem_0_write),
    .in2(store_check_3_mem_0_write), .in3(store_check_4_mem_0_write));
  Clock clock_4 (.out(clock_4_out));
  RAM #(.addrWidth(6), .dataWidth(16)) u_ram_2 (
    .addr(demultiplexer_1_out0), .we(xor_2_out), .oe(1'b1), .clk(clock_5_out), .din(demultiplexer_3_out1),
    .dout(RAM_1));
  ExactlyOne xor_2 (
    .out(xor_2_out), .in0(store_check_1_mem_1_write), .in1(store_check_2_mem_1_write),
    .in2(store_check_3_mem_1_write), .in3(store_check_4_mem_1_write));
  Clock clock_5 (.out(clock_5_out));
  RAM #(.addrWidth(6), .dataWidth(16)) u_ram_3 (
    .addr(demultiplexer_1_out0), .we(xor_3_out), .oe(1'b1), .clk(clock_6_out), .din(demultiplexer_3_out2),
    .dout(RAM_2));
  ExactlyOne xor_3 (
    .out(xor_3_out), .in0(store_check_1_mem_2_write), .in1(store_check_2_mem_2_write),
    .in2(store_check_3_mem_2_write), .in3(store_check_4_mem_2_write));
  Clock clock_6 (.out(clock_6_out));
  RAM #(.addrWidth(6), .dataWidth(16)) ram_4 (
    .addr(demultiplexer_1_out0), .we(xor_4_out), .oe(1'b1), .clk(clock_7_out), .din(demultiplexer_3_out3),
    .dout(RAM_3));
  ExactlyOne xor_4 (
    .out(xor_4_out), .in0(store_check_1_mem_3_write), .in1(store_check_2_mem_3_write),
    .in2(store_check_3_mem_3_write), .in3(store_check_4_mem_3_write));
  Clock clock_7 (.out(clock_7_out));
  Multiplexer #(.disabled("Z"), .width(6)) multiplexer_5 (
    .in1(bitselector_9_out), .out(demultiplexer_1_out0), .sel(comparator_10_eq));  // open: in0
  BitSelector #(.group(6)) bitselector_9 (.in(ROM_0[23:16]), .out(bitselector_9_out), .sel(1'b0));
  Comparator comparator_10 (.a(ROM_0[31:24]), .b(8'hc1), .eq(comparator_10_eq));  // open: gt, lt
  Clock clock_8 (.out(clock_8_out));
  Vector_Unit vector_unit_1 (
    .OPCODE(ROM_0[31:24]), .R0(RAM_0), .R1(RAM_1), .R2(RAM_2), .R3(RAM_3), .Vk(ROM_0[7:0]), .Vj(ROM_0[15:8]),
    .Vi(ROM_0[23:16]), .CLK(clock_8_out), .V0(out_8), .V1(out_11), .Vj_OUT(vector_unit_1_vj_out),
    .Vi_OUT(vector_unit_1_vi_out));
  Vector_ALU vector_alu_1 (.Vi(vector_unit_1_vj_out), .Vj(vector_unit_1_vi_out), .DOT_PROD(out_3));

  assign out_5 = out_3;

  // Notes on the sheet:
  //   contents of CORE_0_ROM (hex, n*v repeats v):
  //   fe000007 70000 70001 70002 70003 fe000007 fe000007 a000804 a010a05 2040506 41060000 fe000007
  //   fe000007 fe000007 c1000000 241*fe000007
  //   contents of CORE_1_ROM (hex, n*v repeats v):
  //   5*fe00000f 70008 70009 7000a 7000b a00090c a010b0d 20c0d0e 410e0001 243*fe00000f
  //   contents of CORE_2_ROM (hex, n*v repeats v):
  //   7*fe000017 a020810 a030a11 2101116 41160002 245*fe000017
  //   contents of CORE_3_ROM (hex, n*v repeats v):
  //   8*fe00001f a020918 a030b19 218191e 411e0003 244*fe00001f
endmodule

module Registers (
  input  [15:0] OVERFLOW_0,
  input  WRITE_ENABLE_1,
  input  WRITE_ENABLE_2,
  input  WRITE_ENABLE_3,
  input  [7:0] Rk_DEMUX_1,
  input  [15:0] DATA_IN_1,
  input  [7:0] Rk_DEMUX_2,
  input  [15:0] DATA_IN_2,
  input  [7:0] Rk_DEMUX_3,
  input  [15:0] DATA_IN_3,
  input  [7:0] Rj_MUX_0,
  input  [7:0] Rj_MUX_1,
  input  [7:0] Rj_MUX_2,
  input  [7:0] Rj_MUX_3,
  input  [7:0] Ri_MUX_0,
  input  [7:0] Ri_MUX_1,
  input  [7:0] Ri_MUX_2,
  input  WRITE_ENABLE_0,
  input  [15:0] DATA_IN_0,
  input  [15:0] OVERFLOW_1,
  input  [7:0] Rk_DEMUX_0,
  input  [7:0] Ri_MUX_3,
  input  [15:0] OVERFLOW_2,
  input  [15:0] OVERFLOW_3,
  input  CLOCK,
  output [15:0] Rj_OUT_0,
  output [15:0] Rj_OUT_1,
  output [15:0] Rj_OUT_2,
  output [15:0] Rj_OUT_3,
  output [15:0] Ri_OUT_0,
  output [15:0] Ri_OUT_1,
  output [15:0] Ri_OUT_2,
  output [15:0] A0,
  output [15:0] A1,
  output [15:0] A2,
  output [15:0] A3,
  output [15:0] A4,
  output [15:0] A5,
  output [15:0] A6,
  output [15:0] A7,
  output [15:0] A8,
  output [15:0] A9,
  output [15:0] AA,
  output [15:0] AB,
  output [15:0] AC,
  output [15:0] AD,
  output [15:0] AE,
  output [15:0] AF,
  output [15:0] Ri_OUT_3,
  output [15:0] B0,
  output [15:0] B1,
  output [15:0] B2,
  output [15:0] B3,
  output [15:0] B4,
  output [15:0] B5,
  output [15:0] B6,
  output [15:0] B7,
  output [15:0] B8,
  output [15:0] B9,
  output [15:0] BA,
  output [15:0] BB,
  output [15:0] BC,
  output [15:0] BD,
  output [15:0] BE,
  output [15:0] BF
);

  wire demultiplexer_1_out0, demultiplexer_1_out1, demultiplexer_1_out2, demultiplexer_1_out3,
       demultiplexer_1_out4, demultiplexer_1_out5, demultiplexer_1_out6, demultiplexer_1_out7,
       demultiplexer_1_out8, demultiplexer_1_out9, demultiplexer_1_out10, demultiplexer_1_out11,
       demultiplexer_1_out12, demultiplexer_1_out13, demultiplexer_1_out14, demultiplexer_1_out15,
       demultiplexer_1_out16, demultiplexer_1_out17, demultiplexer_1_out18, demultiplexer_1_out19,
       demultiplexer_1_out20, demultiplexer_1_out21, demultiplexer_1_out22, demultiplexer_1_out23,
       demultiplexer_1_out24, demultiplexer_1_out25, demultiplexer_1_out26, demultiplexer_1_out27,
       demultiplexer_1_out28, demultiplexer_1_out29, demultiplexer_1_out30, demultiplexer_1_out31;
  wire [4:0] bitselector_1_out, bitselector_2_out, bitselector_3_out, bitselector_4_out, bitselector_5_out,
       bitselector_6_out, bitselector_7_out, bitselector_8_out, bitselector_9_out, bitselector_10_out,
       bitselector_11_out, bitselector_12_out;
  wire [15:0] demultiplexer_5_out0, demultiplexer_5_out1, demultiplexer_5_out2, demultiplexer_5_out3,
       demultiplexer_5_out4, demultiplexer_5_out5, demultiplexer_5_out6, demultiplexer_5_out7,
       demultiplexer_5_out8, demultiplexer_5_out9, demultiplexer_5_out10, demultiplexer_5_out11,
       demultiplexer_5_out12, demultiplexer_5_out13, demultiplexer_5_out14, demultiplexer_5_out15,
       demultiplexer_5_out16, demultiplexer_5_out17, demultiplexer_5_out18, demultiplexer_5_out19,
       demultiplexer_5_out20, demultiplexer_5_out21, demultiplexer_5_out22, demultiplexer_5_out23,
       demultiplexer_5_out24, demultiplexer_5_out25, demultiplexer_5_out26, demultiplexer_5_out27,
       demultiplexer_5_out28, demultiplexer_5_out29, demultiplexer_5_out30, demultiplexer_5_out31;

  Demultiplexer #(.disabled("Z"), .select(5)) demultiplexer_1 (
    .out0(demultiplexer_1_out0), .out1(demultiplexer_1_out1), .out2(demultiplexer_1_out2),
    .out3(demultiplexer_1_out3), .out4(demultiplexer_1_out4), .out5(demultiplexer_1_out5),
    .out6(demultiplexer_1_out6), .out7(demultiplexer_1_out7), .out8(demultiplexer_1_out8),
    .out9(demultiplexer_1_out9), .out10(demultiplexer_1_out10), .out11(demultiplexer_1_out11),
    .out12(demultiplexer_1_out12), .out13(demultiplexer_1_out13), .out14(demultiplexer_1_out14),
    .out15(demultiplexer_1_out15), .out16(demultiplexer_1_out16), .out17(demultiplexer_1_out17),
    .out18(demultiplexer_1_out18), .out19(demultiplexer_1_out19), .out20(demultiplexer_1_out20),
    .out21(demultiplexer_1_out21), .out22(demultiplexer_1_out22), .out23(demultiplexer_1_out23),
    .out24(demultiplexer_1_out24), .out25(demultiplexer_1_out25), .out26(demultiplexer_1_out26),
    .out27(demultiplexer_1_out27), .out28(demultiplexer_1_out28), .out29(demultiplexer_1_out29),
    .out30(demultiplexer_1_out30), .out31(demultiplexer_1_out31), .in(WRITE_ENABLE_0), .sel(bitselector_1_out));
  Demultiplexer #(.disabled("Z"), .select(5), .tristate("true")) demultiplexer_2 (
    .out0(demultiplexer_1_out0), .out1(demultiplexer_1_out1), .out2(demultiplexer_1_out2),
    .out3(demultiplexer_1_out3), .out4(demultiplexer_1_out4), .out5(demultiplexer_1_out5),
    .out6(demultiplexer_1_out6), .out7(demultiplexer_1_out7), .out8(demultiplexer_1_out8),
    .out9(demultiplexer_1_out9), .out10(demultiplexer_1_out10), .out11(demultiplexer_1_out11),
    .out12(demultiplexer_1_out12), .out13(demultiplexer_1_out13), .out14(demultiplexer_1_out14),
    .out15(demultiplexer_1_out15), .out16(demultiplexer_1_out16), .out17(demultiplexer_1_out17),
    .out18(demultiplexer_1_out18), .out19(demultiplexer_1_out19), .out20(demultiplexer_1_out20),
    .out21(demultiplexer_1_out21), .out22(demultiplexer_1_out22), .out23(demultiplexer_1_out23),
    .out24(demultiplexer_1_out24), .out25(demultiplexer_1_out25), .out26(demultiplexer_1_out26),
    .out27(demultiplexer_1_out27), .out28(demultiplexer_1_out28), .out29(demultiplexer_1_out29),
    .out30(demultiplexer_1_out30), .out31(demultiplexer_1_out31), .in(WRITE_ENABLE_1), .sel(bitselector_2_out));
  Demultiplexer #(.disabled("Z"), .select(5), .tristate("true")) demultiplexer_3 (
    .out0(demultiplexer_1_out0), .out1(demultiplexer_1_out1), .out2(demultiplexer_1_out2),
    .out3(demultiplexer_1_out3), .out4(demultiplexer_1_out4), .out5(demultiplexer_1_out5),
    .out6(demultiplexer_1_out6), .out7(demultiplexer_1_out7), .out8(demultiplexer_1_out8),
    .out9(demultiplexer_1_out9), .out10(demultiplexer_1_out10), .out11(demultiplexer_1_out11),
    .out12(demultiplexer_1_out12), .out13(demultiplexer_1_out13), .out14(demultiplexer_1_out14),
    .out15(demultiplexer_1_out15), .out16(demultiplexer_1_out16), .out17(demultiplexer_1_out17),
    .out18(demultiplexer_1_out18), .out19(demultiplexer_1_out19), .out20(demultiplexer_1_out20),
    .out21(demultiplexer_1_out21), .out22(demultiplexer_1_out22), .out23(demultiplexer_1_out23),
    .out24(demultiplexer_1_out24), .out25(demultiplexer_1_out25), .out26(demultiplexer_1_out26),
    .out27(demultiplexer_1_out27), .out28(demultiplexer_1_out28), .out29(demultiplexer_1_out29),
    .out30(demultiplexer_1_out30), .out31(demultiplexer_1_out31), .in(WRITE_ENABLE_2), .sel(bitselector_3_out));
  Demultiplexer #(.disabled("Z"), .select(5), .tristate("true")) demultiplexer_4 (
    .out0(demultiplexer_1_out0), .out1(demultiplexer_1_out1), .out2(demultiplexer_1_out2),
    .out3(demultiplexer_1_out3), .out4(demultiplexer_1_out4), .out5(demultiplexer_1_out5),
    .out6(demultiplexer_1_out6), .out7(demultiplexer_1_out7), .out8(demultiplexer_1_out8),
    .out9(demultiplexer_1_out9), .out10(demultiplexer_1_out10), .out11(demultiplexer_1_out11),
    .out12(demultiplexer_1_out12), .out13(demultiplexer_1_out13), .out14(demultiplexer_1_out14),
    .out15(demultiplexer_1_out15), .out16(demultiplexer_1_out16), .out17(demultiplexer_1_out17),
    .out18(demultiplexer_1_out18), .out19(demultiplexer_1_out19), .out20(demultiplexer_1_out20),
    .out21(demultiplexer_1_out21), .out22(demultiplexer_1_out22), .out23(demultiplexer_1_out23),
    .out24(demultiplexer_1_out24), .out25(demultiplexer_1_out25), .out26(demultiplexer_1_out26),
    .out27(demultiplexer_1_out27), .out28(demultiplexer_1_out28), .out29(demultiplexer_1_out29),
    .out30(demultiplexer_1_out30), .out31(demultiplexer_1_out31), .in(WRITE_ENABLE_3), .sel(bitselector_4_out));
  Demultiplexer #(.disabled("Z"), .select(5), .tristate("true"), .width(16)) demultiplexer_5 (
    .out0(demultiplexer_5_out0), .out1(demultiplexer_5_out1), .out2(demultiplexer_5_out2),
    .out3(demultiplexer_5_out3), .out4(demultiplexer_5_out4), .out5(demultiplexer_5_out5),
    .out6(demultiplexer_5_out6), .out7(demultiplexer_5_out7), .out8(demultiplexer_5_out8),
    .out9(demultiplexer_5_out9), .out10(demultiplexer_5_out10), .out11(demultiplexer_5_out11),
    .out12(demultiplexer_5_out12), .out13(demultiplexer_5_out13), .out14(demultiplexer_5_out14),
    .out15(demultiplexer_5_out15), .out16(demultiplexer_5_out16), .out17(demultiplexer_5_out17),
    .out18(demultiplexer_5_out18), .out19(demultiplexer_5_out19), .out20(demultiplexer_5_out20),
    .out21(demultiplexer_5_out21), .out22(demultiplexer_5_out22), .out23(demultiplexer_5_out23),
    .out24(demultiplexer_5_out24), .out25(demultiplexer_5_out25), .out26(demultiplexer_5_out26),
    .out27(demultiplexer_5_out27), .out28(demultiplexer_5_out28), .out29(demultiplexer_5_out29),
    .out30(demultiplexer_5_out30), .out31(demultiplexer_5_out31), .in(DATA_IN_0), .sel(bitselector_1_out));
  BitSelector #(.group(5)) bitselector_1 (.in(Rk_DEMUX_0), .out(bitselector_1_out), .sel(1'b0));
  BitSelector #(.group(5)) bitselector_2 (.in(Rk_DEMUX_1), .out(bitselector_2_out), .sel(1'b0));
  Demultiplexer #(.disabled("Z"), .select(5), .tristate("true"), .width(16)) demultiplexer_6 (
    .out0(demultiplexer_5_out0), .out1(demultiplexer_5_out1), .out2(demultiplexer_5_out2),
    .out3(demultiplexer_5_out3), .out4(demultiplexer_5_out4), .out5(demultiplexer_5_out5),
    .out6(demultiplexer_5_out6), .out7(demultiplexer_5_out7), .out8(demultiplexer_5_out8),
    .out9(demultiplexer_5_out9), .out10(demultiplexer_5_out10), .out11(demultiplexer_5_out11),
    .out12(demultiplexer_5_out12), .out13(demultiplexer_5_out13), .out14(demultiplexer_5_out14),
    .out15(demultiplexer_5_out15), .out16(demultiplexer_5_out16), .out17(demultiplexer_5_out17),
    .out18(demultiplexer_5_out18), .out19(demultiplexer_5_out19), .out20(demultiplexer_5_out20),
    .out21(demultiplexer_5_out21), .out22(demultiplexer_5_out22), .out23(demultiplexer_5_out23),
    .out24(demultiplexer_5_out24), .out25(demultiplexer_5_out25), .out26(demultiplexer_5_out26),
    .out27(demultiplexer_5_out27), .out28(demultiplexer_5_out28), .out29(demultiplexer_5_out29),
    .out30(demultiplexer_5_out30), .out31(demultiplexer_5_out31), .in(DATA_IN_1), .sel(bitselector_2_out));
  BitSelector #(.group(5)) bitselector_3 (.in(Rk_DEMUX_2), .out(bitselector_3_out), .sel(1'b0));
  Demultiplexer #(.disabled("Z"), .select(5), .tristate("true"), .width(16)) demultiplexer_7 (
    .out0(demultiplexer_5_out0), .out1(demultiplexer_5_out1), .out2(demultiplexer_5_out2),
    .out3(demultiplexer_5_out3), .out4(demultiplexer_5_out4), .out5(demultiplexer_5_out5),
    .out6(demultiplexer_5_out6), .out7(demultiplexer_5_out7), .out8(demultiplexer_5_out8),
    .out9(demultiplexer_5_out9), .out10(demultiplexer_5_out10), .out11(demultiplexer_5_out11),
    .out12(demultiplexer_5_out12), .out13(demultiplexer_5_out13), .out14(demultiplexer_5_out14),
    .out15(demultiplexer_5_out15), .out16(demultiplexer_5_out16), .out17(demultiplexer_5_out17),
    .out18(demultiplexer_5_out18), .out19(demultiplexer_5_out19), .out20(demultiplexer_5_out20),
    .out21(demultiplexer_5_out21), .out22(demultiplexer_5_out22), .out23(demultiplexer_5_out23),
    .out24(demultiplexer_5_out24), .out25(demultiplexer_5_out25), .out26(demultiplexer_5_out26),
    .out27(demultiplexer_5_out27), .out28(demultiplexer_5_out28), .out29(demultiplexer_5_out29),
    .out30(demultiplexer_5_out30), .out31(demultiplexer_5_out31), .in(DATA_IN_2), .sel(bitselector_3_out));
  BitSelector #(.group(5)) bitselector_4 (.in(Rk_DEMUX_3), .out(bitselector_4_out), .sel(1'b0));
  Demultiplexer #(.disabled("Z"), .select(5), .tristate("true"), .width(16)) demultiplexer_8 (
    .out0(demultiplexer_5_out0), .out1(demultiplexer_5_out1), .out2(demultiplexer_5_out2),
    .out3(demultiplexer_5_out3), .out4(demultiplexer_5_out4), .out5(demultiplexer_5_out5),
    .out6(demultiplexer_5_out6), .out7(demultiplexer_5_out7), .out8(demultiplexer_5_out8),
    .out9(demultiplexer_5_out9), .out10(demultiplexer_5_out10), .out11(demultiplexer_5_out11),
    .out12(demultiplexer_5_out12), .out13(demultiplexer_5_out13), .out14(demultiplexer_5_out14),
    .out15(demultiplexer_5_out15), .out16(demultiplexer_5_out16), .out17(demultiplexer_5_out17),
    .out18(demultiplexer_5_out18), .out19(demultiplexer_5_out19), .out20(demultiplexer_5_out20),
    .out21(demultiplexer_5_out21), .out22(demultiplexer_5_out22), .out23(demultiplexer_5_out23),
    .out24(demultiplexer_5_out24), .out25(demultiplexer_5_out25), .out26(demultiplexer_5_out26),
    .out27(demultiplexer_5_out27), .out28(demultiplexer_5_out28), .out29(demultiplexer_5_out29),
    .out30(demultiplexer_5_out30), .out31(demultiplexer_5_out31), .in(DATA_IN_3), .sel(bitselector_4_out));
  Register #(.width(16)) register_1 (
    .D(demultiplexer_5_out0), .en(demultiplexer_1_out0), .clk(CLOCK), .Q(A0));  // open: clr
  Register #(.width(16)) register_2 (
    .D(demultiplexer_5_out1), .en(demultiplexer_1_out1), .clk(CLOCK), .Q(A1));  // open: clr
  Register #(.width(16)) register_3 (
    .D(demultiplexer_5_out2), .en(demultiplexer_1_out2), .clk(CLOCK), .Q(A2));  // open: clr
  Register #(.width(16)) register_4 (
    .D(demultiplexer_5_out3), .en(demultiplexer_1_out3), .clk(CLOCK), .Q(A3));  // open: clr
  Register #(.width(16)) register_5 (
    .D(demultiplexer_5_out4), .en(demultiplexer_1_out4), .clk(CLOCK), .Q(A4));  // open: clr
  Register #(.width(16)) register_6 (
    .D(demultiplexer_5_out5), .en(demultiplexer_1_out5), .clk(CLOCK), .Q(A5));  // open: clr
  Register #(.width(16)) register_7 (
    .D(demultiplexer_5_out6), .en(demultiplexer_1_out6), .clk(CLOCK), .Q(A6));  // open: clr
  Register #(.width(16)) register_8 (.D(OVERFLOW_0), .en(1'b1), .clk(CLOCK), .Q(A7));  // open: clr
  Register #(.width(16)) register_9 (
    .D(demultiplexer_5_out8), .en(demultiplexer_1_out8), .clk(CLOCK), .Q(A8));  // open: clr
  Register #(.width(16)) register_10 (
    .D(demultiplexer_5_out9), .en(demultiplexer_1_out9), .clk(CLOCK), .Q(A9));  // open: clr
  Register #(.width(16)) register_11 (
    .D(demultiplexer_5_out10), .en(demultiplexer_1_out10), .clk(CLOCK), .Q(AA));  // open: clr
  Register #(.width(16)) register_12 (
    .D(demultiplexer_5_out11), .en(demultiplexer_1_out11), .clk(CLOCK), .Q(AB));  // open: clr
  Register #(.width(16)) register_13 (
    .D(demultiplexer_5_out12), .en(demultiplexer_1_out12), .clk(CLOCK), .Q(AC));  // open: clr
  Register #(.width(16)) register_14 (
    .D(demultiplexer_5_out13), .en(demultiplexer_1_out13), .clk(CLOCK), .Q(AD));  // open: clr
  Register #(.width(16)) register_15 (
    .D(demultiplexer_5_out14), .en(demultiplexer_1_out14), .clk(CLOCK), .Q(AE));  // open: clr
  Register #(.width(16)) register_16 (.D(OVERFLOW_1), .en(1'b1), .clk(CLOCK), .Q(AF));  // open: clr
  Register #(.width(16)) register_17 (
    .D(demultiplexer_5_out16), .en(demultiplexer_1_out16), .clk(CLOCK), .Q(B0));  // open: clr
  Register #(.width(16)) register_18 (
    .D(demultiplexer_5_out17), .en(demultiplexer_1_out17), .clk(CLOCK), .Q(B1));  // open: clr
  Register #(.width(16)) register_19 (
    .D(demultiplexer_5_out18), .en(demultiplexer_1_out18), .clk(CLOCK), .Q(B2));  // open: clr
  Register #(.width(16)) register_20 (
    .D(demultiplexer_5_out19), .en(demultiplexer_1_out19), .clk(CLOCK), .Q(B3));  // open: clr
  Register #(.width(16)) register_21 (
    .D(demultiplexer_5_out20), .en(demultiplexer_1_out20), .clk(CLOCK), .Q(B4));  // open: clr
  Register #(.width(16)) register_22 (
    .D(demultiplexer_5_out21), .en(demultiplexer_1_out21), .clk(CLOCK), .Q(B5));  // open: clr
  Register #(.width(16)) register_23 (
    .D(demultiplexer_5_out22), .en(demultiplexer_1_out22), .clk(CLOCK), .Q(B6));  // open: clr
  Register #(.width(16)) register_24 (.D(OVERFLOW_2), .en(1'b1), .clk(CLOCK), .Q(B7));  // open: clr
  Register #(.width(16)) register_25 (
    .D(demultiplexer_5_out24), .en(demultiplexer_1_out24), .clk(CLOCK), .Q(B8));  // open: clr
  Register #(.width(16)) register_26 (
    .D(demultiplexer_5_out25), .en(demultiplexer_1_out25), .clk(CLOCK), .Q(B9));  // open: clr
  Register #(.width(16)) register_27 (
    .D(demultiplexer_5_out26), .en(demultiplexer_1_out26), .clk(CLOCK), .Q(BA));  // open: clr
  Register #(.width(16)) register_28 (
    .D(demultiplexer_5_out27), .en(demultiplexer_1_out27), .clk(CLOCK), .Q(BB));  // open: clr
  Register #(.width(16)) register_29 (
    .D(demultiplexer_5_out28), .en(demultiplexer_1_out28), .clk(CLOCK), .Q(BC));  // open: clr
  Register #(.width(16)) register_30 (
    .D(demultiplexer_5_out29), .en(demultiplexer_1_out29), .clk(CLOCK), .Q(BD));  // open: clr
  Register #(.width(16)) register_31 (
    .D(demultiplexer_5_out30), .en(demultiplexer_1_out30), .clk(CLOCK), .Q(BE));  // open: clr
  Register #(.width(16)) register_32 (.D(OVERFLOW_3), .en(1'b1), .clk(CLOCK), .Q(BF));  // open: clr
  BitSelector #(.group(5)) bitselector_5 (.in(Rj_MUX_0), .out(bitselector_5_out), .sel(1'b0));
  Multiplexer #(.select(5), .width(16)) multiplexer_1 (
    .in0(A0), .in1(A1), .in2(A2), .in3(A3), .in4(A4), .in5(A5), .in6(A6), .in7(A7), .in8(A8), .in9(A9),
    .in10(AA), .in11(AB), .in12(AC), .in13(AD), .in14(AE), .in15(AF), .in16(B0), .in17(B1), .in18(B2),
    .in19(B3), .in20(B4), .in21(B5), .in22(B6), .in23(B7), .in24(B8), .in25(B9), .in26(BA), .in27(BB),
    .in28(BC), .in29(BD), .in30(BE), .in31(BF), .out(Rj_OUT_0), .sel(bitselector_5_out));
  BitSelector #(.group(5)) bitselector_6 (.in(Rj_MUX_1), .out(bitselector_6_out), .sel(1'b0));
  Multiplexer #(.select(5), .width(16)) multiplexer_2 (
    .in0(A0), .in1(A1), .in2(A2), .in3(A3), .in4(A4), .in5(A5), .in6(A6), .in7(A7), .in8(A8), .in9(A9),
    .in10(AA), .in11(AB), .in12(AC), .in13(AD), .in14(AE), .in15(AF), .in16(B0), .in17(B1), .in18(B2),
    .in19(B3), .in20(B4), .in21(B5), .in22(B6), .in23(B7), .in24(B8), .in25(B9), .in26(BA), .in27(BB),
    .in28(BC), .in29(BD), .in30(BE), .in31(BF), .out(Rj_OUT_1), .sel(bitselector_6_out));
  BitSelector #(.group(5)) bitselector_7 (.in(Rj_MUX_2), .out(bitselector_7_out), .sel(1'b0));
  Multiplexer #(.select(5), .width(16)) multiplexer_3 (
    .in0(A0), .in1(A1), .in2(A2), .in3(A3), .in4(A4), .in5(A5), .in6(A6), .in7(A7), .in8(A8), .in9(A9),
    .in10(AA), .in11(AB), .in12(AC), .in13(AD), .in14(AE), .in15(AF), .in16(B0), .in17(B1), .in18(B2),
    .in19(B3), .in20(B4), .in21(B5), .in22(B6), .in23(B7), .in24(B8), .in25(B9), .in26(BA), .in27(BB),
    .in28(BC), .in29(BD), .in30(BE), .in31(BF), .out(Rj_OUT_2), .sel(bitselector_7_out));
  BitSelector #(.group(5)) bitselector_8 (.in(Rj_MUX_3), .out(bitselector_8_out), .sel(1'b0));
  Multiplexer #(.select(5), .width(16)) multiplexer_4 (
    .in0(A0), .in1(A1), .in2(A2), .in3(A3), .in4(A4), .in5(A5), .in6(A6), .in7(A7), .in8(A8), .in9(A9),
    .in10(AA), .in11(AB), .in12(AC), .in13(AD), .in14(AE), .in15(AF), .in16(B0), .in17(B1), .in18(B2),
    .in19(B3), .in20(B4), .in21(B5), .in22(B6), .in23(B7), .in24(B8), .in25(B9), .in26(BA), .in27(BB),
    .in28(BC), .in29(BD), .in30(BE), .in31(BF), .out(Rj_OUT_3), .sel(bitselector_8_out));
  BitSelector #(.group(5)) bitselector_9 (.in(Ri_MUX_0), .out(bitselector_9_out), .sel(1'b0));
  Multiplexer #(.select(5), .width(16)) multiplexer_5 (
    .in0(A0), .in1(A1), .in2(A2), .in3(A3), .in4(A4), .in5(A5), .in6(A6), .in7(A7), .in8(A8), .in9(A9),
    .in10(AA), .in11(AB), .in12(AC), .in13(AD), .in14(AE), .in15(AF), .in16(B0), .in17(B1), .in18(B2),
    .in19(B3), .in20(B4), .in21(B5), .in22(B6), .in23(B7), .in24(B8), .in25(B9), .in26(BA), .in27(BB),
    .in28(BC), .in29(BD), .in30(BE), .in31(BF), .out(Ri_OUT_0), .sel(bitselector_9_out));
  BitSelector #(.group(5)) bitselector_10 (.in(Ri_MUX_1), .out(bitselector_10_out), .sel(1'b0));
  Multiplexer #(.select(5), .width(16)) multiplexer_6 (
    .in0(A0), .in1(A1), .in2(A2), .in3(A3), .in4(A4), .in5(A5), .in6(A6), .in7(A7), .in8(A8), .in9(A9),
    .in10(AA), .in11(AB), .in12(AC), .in13(AD), .in14(AE), .in15(AF), .in16(B0), .in17(B1), .in18(B2),
    .in19(B3), .in20(B4), .in21(B5), .in22(B6), .in23(B7), .in24(B8), .in25(B9), .in26(BA), .in27(BB),
    .in28(BC), .in29(BD), .in30(BE), .in31(BF), .out(Ri_OUT_1), .sel(bitselector_10_out));
  BitSelector #(.group(5)) bitselector_11 (.in(Ri_MUX_2), .out(bitselector_11_out), .sel(1'b0));
  Multiplexer #(.select(5), .width(16)) multiplexer_7 (
    .in0(A0), .in1(A1), .in2(A2), .in3(A3), .in4(A4), .in5(A5), .in6(A6), .in7(A7), .in8(A8), .in9(A9),
    .in10(AA), .in11(AB), .in12(AC), .in13(AD), .in14(AE), .in15(AF), .in16(B0), .in17(B1), .in18(B2),
    .in19(B3), .in20(B4), .in21(B5), .in22(B6), .in23(B7), .in24(B8), .in25(B9), .in26(BA), .in27(BB),
    .in28(BC), .in29(BD), .in30(BE), .in31(BF), .out(Ri_OUT_2), .sel(bitselector_11_out));
  BitSelector #(.group(5)) bitselector_12 (.in(Ri_MUX_3), .out(bitselector_12_out), .sel(1'b0));
  Multiplexer #(.select(5), .width(16)) multiplexer_8 (
    .in0(A0), .in1(A1), .in2(A2), .in3(A3), .in4(A4), .in5(A5), .in6(A6), .in7(A7), .in8(A8), .in9(A9),
    .in10(AA), .in11(AB), .in12(AC), .in13(AD), .in14(AE), .in15(AF), .in16(B0), .in17(B1), .in18(B2),
    .in19(B3), .in20(B4), .in21(B5), .in22(B6), .in23(B7), .in24(B8), .in25(B9), .in26(BA), .in27(BB),
    .in28(BC), .in29(BD), .in30(BE), .in31(BF), .out(Ri_OUT_3), .sel(bitselector_12_out));
endmodule

module Registers_test (
  input  [4:0] Rj_MUX,
  input  [4:0] Ri_MUX,
  output [15:0] Rj_OUT,
  output [15:0] A0,
  output [15:0] A1,
  output [15:0] A2,
  output [15:0] A3,
  output [15:0] A4,
  output [15:0] A5,
  output [15:0] A6,
  output [15:0] A7,
  output [15:0] A8,
  output [15:0] A9,
  output [15:0] AA,
  output [15:0] AB,
  output [15:0] AC,
  output [15:0] AD,
  output [15:0] AE,
  output [15:0] AF,
  output [15:0] Ri_OUT,
  output [15:0] B0,
  output [15:0] B1,
  output [15:0] B2,
  output [15:0] B3,
  output [15:0] B4,
  output [15:0] B5,
  output [15:0] B6,
  output [15:0] B7,
  output [15:0] B8,
  output [15:0] B9,
  output [15:0] BA,
  output [15:0] BB,
  output [15:0] BC,
  output [15:0] BD,
  output [15:0] BE,
  output [15:0] BF
);

  wire clock_1_out, comparator_1_gt, comparator_2_gt, comparator_3_gt, comparator_4_gt, comparator_5_gt,
       comparator_6_gt, comparator_7_gt, comparator_8_gt, comparator_9_gt, comparator_10_gt,
       comparator_11_gt, comparator_12_gt, comparator_13_gt, comparator_14_gt, comparator_15_gt,
       comparator_16_gt, comparator_17_gt, comparator_18_gt, comparator_19_gt, comparator_20_gt,
       comparator_21_gt, comparator_22_gt, comparator_23_gt, comparator_24_gt, comparator_25_gt,
       comparator_26_gt, comparator_27_gt, comparator_28_gt, comparator_29_gt, comparator_30_gt,
       comparator_31_gt, comparator_32_gt;
  wire [15:0] demultiplexer_1_out0, demultiplexer_1_out1, demultiplexer_1_out2, demultiplexer_1_out3,
       demultiplexer_1_out4, demultiplexer_1_out5, demultiplexer_1_out6, demultiplexer_1_out7,
       demultiplexer_1_out8, demultiplexer_1_out9, demultiplexer_1_out10, demultiplexer_1_out11,
       demultiplexer_1_out12, demultiplexer_1_out13, demultiplexer_1_out14, demultiplexer_1_out15,
       demultiplexer_1_out16, demultiplexer_1_out17, demultiplexer_1_out18, demultiplexer_1_out19,
       demultiplexer_1_out20, demultiplexer_1_out21, demultiplexer_1_out22, demultiplexer_1_out23,
       demultiplexer_1_out24, demultiplexer_1_out25, demultiplexer_1_out26, demultiplexer_1_out27,
       demultiplexer_1_out28, demultiplexer_1_out29, demultiplexer_1_out30, demultiplexer_1_out31;

  Demultiplexer #(.select(5), .width(16)) demultiplexer_1 (
    .out0(demultiplexer_1_out0), .out1(demultiplexer_1_out1), .out2(demultiplexer_1_out2),
    .out3(demultiplexer_1_out3), .out4(demultiplexer_1_out4), .out5(demultiplexer_1_out5),
    .out6(demultiplexer_1_out6), .out7(demultiplexer_1_out7), .out8(demultiplexer_1_out8),
    .out9(demultiplexer_1_out9), .out10(demultiplexer_1_out10), .out11(demultiplexer_1_out11),
    .out12(demultiplexer_1_out12), .out13(demultiplexer_1_out13), .out14(demultiplexer_1_out14),
    .out15(demultiplexer_1_out15), .out16(demultiplexer_1_out16), .out17(demultiplexer_1_out17),
    .out18(demultiplexer_1_out18), .out19(demultiplexer_1_out19), .out20(demultiplexer_1_out20),
    .out21(demultiplexer_1_out21), .out22(demultiplexer_1_out22), .out23(demultiplexer_1_out23),
    .out24(demultiplexer_1_out24), .out25(demultiplexer_1_out25), .out26(demultiplexer_1_out26),
    .out27(demultiplexer_1_out27), .out28(demultiplexer_1_out28), .out29(demultiplexer_1_out29),
    .out30(demultiplexer_1_out30), .out31(demultiplexer_1_out31), .in(16'h8008), .sel(5'b00011));
  Register #(.width(16)) register_1 (
    .D(demultiplexer_1_out0), .en(comparator_1_gt), .clk(clock_1_out), .Q(A0));  // open: clr
  Comparator #(.mode("unsigned"), .width(16)) comparator_1 (
    .a(demultiplexer_1_out0), .b({16{1'b0}}), .gt(comparator_1_gt));  // open: eq, lt
  Register #(.width(16)) register_2 (
    .D(demultiplexer_1_out1), .en(comparator_2_gt), .clk(clock_1_out), .Q(A1));  // open: clr
  Comparator #(.mode("unsigned"), .width(16)) comparator_2 (
    .a(demultiplexer_1_out1), .b({16{1'b0}}), .gt(comparator_2_gt));  // open: eq, lt
  Register #(.width(16)) register_3 (
    .D(demultiplexer_1_out2), .en(comparator_3_gt), .clk(clock_1_out), .Q(A2));  // open: clr
  Comparator #(.mode("unsigned"), .width(16)) comparator_3 (
    .a(demultiplexer_1_out2), .b({16{1'b0}}), .gt(comparator_3_gt));  // open: eq, lt
  Register #(.width(16)) register_4 (
    .D(demultiplexer_1_out3), .en(comparator_4_gt), .clk(clock_1_out), .Q(A3));  // open: clr
  Comparator #(.mode("unsigned"), .width(16)) comparator_4 (
    .a(demultiplexer_1_out3), .b({16{1'b0}}), .gt(comparator_4_gt));  // open: eq, lt
  Register #(.width(16)) register_5 (
    .D(demultiplexer_1_out4), .en(comparator_5_gt), .clk(clock_1_out), .Q(A4));  // open: clr
  Comparator #(.mode("unsigned"), .width(16)) comparator_5 (
    .a(demultiplexer_1_out4), .b({16{1'b0}}), .gt(comparator_5_gt));  // open: eq, lt
  Register #(.width(16)) register_6 (
    .D(demultiplexer_1_out5), .en(comparator_6_gt), .clk(clock_1_out), .Q(A5));  // open: clr
  Comparator #(.mode("unsigned"), .width(16)) comparator_6 (
    .a(demultiplexer_1_out5), .b({16{1'b0}}), .gt(comparator_6_gt));  // open: eq, lt
  Register #(.width(16)) register_7 (
    .D(demultiplexer_1_out6), .en(comparator_7_gt), .clk(clock_1_out), .Q(A6));  // open: clr
  Comparator #(.mode("unsigned"), .width(16)) comparator_7 (
    .a(demultiplexer_1_out6), .b({16{1'b0}}), .gt(comparator_7_gt));  // open: eq, lt
  Register #(.width(16)) register_8 (
    .D(demultiplexer_1_out7), .en(comparator_8_gt), .clk(clock_1_out), .Q(A7));  // open: clr
  Comparator #(.mode("unsigned"), .width(16)) comparator_8 (
    .a(demultiplexer_1_out7), .b({16{1'b0}}), .gt(comparator_8_gt));  // open: eq, lt
  Register #(.width(16)) register_9 (
    .D(demultiplexer_1_out8), .en(comparator_9_gt), .clk(clock_1_out), .Q(A8));  // open: clr
  Comparator #(.mode("unsigned"), .width(16)) comparator_9 (
    .a(demultiplexer_1_out8), .b({16{1'b0}}), .gt(comparator_9_gt));  // open: eq, lt
  Register #(.width(16)) register_10 (
    .D(demultiplexer_1_out9), .en(comparator_10_gt), .clk(clock_1_out), .Q(A9));  // open: clr
  Comparator #(.mode("unsigned"), .width(16)) comparator_10 (
    .a(demultiplexer_1_out9), .b({16{1'b0}}), .gt(comparator_10_gt));  // open: eq, lt
  Register #(.width(16)) register_11 (
    .D(demultiplexer_1_out10), .en(comparator_11_gt), .clk(clock_1_out), .Q(AA));  // open: clr
  Comparator #(.mode("unsigned"), .width(16)) comparator_11 (
    .a(demultiplexer_1_out10), .b({16{1'b0}}), .gt(comparator_11_gt));  // open: eq, lt
  Register #(.width(16)) register_12 (
    .D(demultiplexer_1_out11), .en(comparator_12_gt), .clk(clock_1_out), .Q(AB));  // open: clr
  Comparator #(.mode("unsigned"), .width(16)) comparator_12 (
    .a(demultiplexer_1_out11), .b({16{1'b0}}), .gt(comparator_12_gt));  // open: eq, lt
  Register #(.width(16)) register_13 (
    .D(demultiplexer_1_out12), .en(comparator_13_gt), .clk(clock_1_out), .Q(AC));  // open: clr
  Comparator #(.mode("unsigned"), .width(16)) comparator_13 (
    .a(demultiplexer_1_out12), .b({16{1'b0}}), .gt(comparator_13_gt));  // open: eq, lt
  Register #(.width(16)) register_14 (
    .D(demultiplexer_1_out13), .en(comparator_14_gt), .clk(clock_1_out), .Q(AD));  // open: clr
  Comparator #(.mode("unsigned"), .width(16)) comparator_14 (
    .a(demultiplexer_1_out13), .b({16{1'b0}}), .gt(comparator_14_gt));  // open: eq, lt
  Register #(.width(16)) register_15 (
    .D(demultiplexer_1_out14), .en(comparator_15_gt), .clk(clock_1_out), .Q(AE));  // open: clr
  Comparator #(.mode("unsigned"), .width(16)) comparator_15 (
    .a(demultiplexer_1_out14), .b({16{1'b0}}), .gt(comparator_15_gt));  // open: eq, lt
  Register #(.width(16)) register_16 (
    .D(demultiplexer_1_out15), .en(comparator_16_gt), .clk(clock_1_out), .Q(AF));  // open: clr
  Comparator #(.mode("unsigned"), .width(16)) comparator_16 (
    .a(demultiplexer_1_out15), .b({16{1'b0}}), .gt(comparator_16_gt));  // open: eq, lt
  Register #(.width(16)) register_17 (
    .D(demultiplexer_1_out16), .en(comparator_17_gt), .clk(clock_1_out), .Q(B0));  // open: clr
  Comparator #(.mode("unsigned"), .width(16)) comparator_17 (
    .a(demultiplexer_1_out16), .b({16{1'b0}}), .gt(comparator_17_gt));  // open: eq, lt
  Register #(.width(16)) register_18 (
    .D(demultiplexer_1_out17), .en(comparator_18_gt), .clk(clock_1_out), .Q(B1));  // open: clr
  Comparator #(.mode("unsigned"), .width(16)) comparator_18 (
    .a(demultiplexer_1_out17), .b({16{1'b0}}), .gt(comparator_18_gt));  // open: eq, lt
  Register #(.width(16)) register_19 (
    .D(demultiplexer_1_out18), .en(comparator_19_gt), .clk(clock_1_out), .Q(B2));  // open: clr
  Comparator #(.mode("unsigned"), .width(16)) comparator_19 (
    .a(demultiplexer_1_out18), .b({16{1'b0}}), .gt(comparator_19_gt));  // open: eq, lt
  Register #(.width(16)) register_20 (
    .D(demultiplexer_1_out19), .en(comparator_20_gt), .clk(clock_1_out), .Q(B3));  // open: clr
  Comparator #(.mode("unsigned"), .width(16)) comparator_20 (
    .a(demultiplexer_1_out19), .b({16{1'b0}}), .gt(comparator_20_gt));  // open: eq, lt
  Register #(.width(16)) register_21 (
    .D(demultiplexer_1_out20), .en(comparator_21_gt), .clk(clock_1_out), .Q(B4));  // open: clr
  Comparator #(.mode("unsigned"), .width(16)) comparator_21 (
    .a(demultiplexer_1_out20), .b({16{1'b0}}), .gt(comparator_21_gt));  // open: eq, lt
  Register #(.width(16)) register_22 (
    .D(demultiplexer_1_out21), .en(comparator_22_gt), .clk(clock_1_out), .Q(B5));  // open: clr
  Comparator #(.mode("unsigned"), .width(16)) comparator_22 (
    .a(demultiplexer_1_out21), .b({16{1'b0}}), .gt(comparator_22_gt));  // open: eq, lt
  Register #(.width(16)) register_23 (
    .D(demultiplexer_1_out22), .en(comparator_23_gt), .clk(clock_1_out), .Q(B6));  // open: clr
  Comparator #(.mode("unsigned"), .width(16)) comparator_23 (
    .a(demultiplexer_1_out22), .b({16{1'b0}}), .gt(comparator_23_gt));  // open: eq, lt
  Register #(.width(16)) register_24 (
    .D(demultiplexer_1_out23), .en(comparator_24_gt), .clk(clock_1_out), .Q(B7));  // open: clr
  Comparator #(.mode("unsigned"), .width(16)) comparator_24 (
    .a(demultiplexer_1_out23), .b({16{1'b0}}), .gt(comparator_24_gt));  // open: eq, lt
  Register #(.width(16)) register_25 (
    .D(demultiplexer_1_out24), .en(comparator_25_gt), .clk(clock_1_out), .Q(B8));  // open: clr
  Comparator #(.mode("unsigned"), .width(16)) comparator_25 (
    .a(demultiplexer_1_out24), .b({16{1'b0}}), .gt(comparator_25_gt));  // open: eq, lt
  Register #(.width(16)) register_26 (
    .D(demultiplexer_1_out25), .en(comparator_26_gt), .clk(clock_1_out), .Q(B9));  // open: clr
  Comparator #(.mode("unsigned"), .width(16)) comparator_26 (
    .a(demultiplexer_1_out25), .b({16{1'b0}}), .gt(comparator_26_gt));  // open: eq, lt
  Register #(.width(16)) register_27 (
    .D(demultiplexer_1_out26), .en(comparator_27_gt), .clk(clock_1_out), .Q(BA));  // open: clr
  Comparator #(.mode("unsigned"), .width(16)) comparator_27 (
    .a(demultiplexer_1_out26), .b({16{1'b0}}), .gt(comparator_27_gt));  // open: eq, lt
  Register #(.width(16)) register_28 (
    .D(demultiplexer_1_out27), .en(comparator_28_gt), .clk(clock_1_out), .Q(BB));  // open: clr
  Comparator #(.mode("unsigned"), .width(16)) comparator_28 (
    .a(demultiplexer_1_out27), .b({16{1'b0}}), .gt(comparator_28_gt));  // open: eq, lt
  Register #(.width(16)) register_29 (
    .D(demultiplexer_1_out28), .en(comparator_29_gt), .clk(clock_1_out), .Q(BC));  // open: clr
  Comparator #(.mode("unsigned"), .width(16)) comparator_29 (
    .a(demultiplexer_1_out28), .b({16{1'b0}}), .gt(comparator_29_gt));  // open: eq, lt
  Register #(.width(16)) register_30 (
    .D(demultiplexer_1_out29), .en(comparator_30_gt), .clk(clock_1_out), .Q(BD));  // open: clr
  Comparator #(.mode("unsigned"), .width(16)) comparator_30 (
    .a(demultiplexer_1_out29), .b({16{1'b0}}), .gt(comparator_30_gt));  // open: eq, lt
  Register #(.width(16)) register_31 (
    .D(demultiplexer_1_out30), .en(comparator_31_gt), .clk(clock_1_out), .Q(BE));  // open: clr
  Comparator #(.mode("unsigned"), .width(16)) comparator_31 (
    .a(demultiplexer_1_out30), .b({16{1'b0}}), .gt(comparator_31_gt));  // open: eq, lt
  Register #(.width(16)) register_32 (
    .D(demultiplexer_1_out31), .en(comparator_32_gt), .clk(clock_1_out), .Q(BF));  // open: clr
  Comparator #(.mode("unsigned"), .width(16)) comparator_32 (
    .a(demultiplexer_1_out31), .b({16{1'b0}}), .gt(comparator_32_gt));  // open: eq, lt
  Clock clock_1 (.out(clock_1_out));
  Multiplexer #(.select(5), .width(16)) multiplexer_1 (
    .in0(A0), .in1(A1), .in2(A2), .in3(A3), .in4(A4), .in5(A5), .in6(A6), .in7(A7), .in8(A8), .in9(A9),
    .in10(AA), .in11(AB), .in12(AC), .in13(AD), .in14(AE), .in15(AF), .in16(B0), .in17(B1), .in18(B2),
    .in19(B3), .in20(B4), .in21(B5), .in22(B6), .in23(B7), .in24(B8), .in25(B9), .in26(BA), .in27(BB),
    .in28(BC), .in29(BD), .in30(BE), .in31(BF), .out(Rj_OUT), .sel(Rj_MUX));
  Multiplexer #(.select(5), .width(16)) multiplexer_2 (
    .in0(A0), .in1(A1), .in2(A2), .in3(A3), .in4(A4), .in5(A5), .in6(A6), .in7(A7), .in8(A8), .in9(A9),
    .in10(AA), .in11(AB), .in12(AC), .in13(AD), .in14(AE), .in15(AF), .in16(B0), .in17(B1), .in18(B2),
    .in19(B3), .in20(B4), .in21(B5), .in22(B6), .in23(B7), .in24(B8), .in25(B9), .in26(BA), .in27(BB),
    .in28(BC), .in29(BD), .in30(BE), .in31(BF), .out(Ri_OUT), .sel(Ri_MUX));
endmodule

module Counters (
  input  CLOCK,
  output [15:0] UP_COUNTER,
  output [15:0] DOWN_COUNTER
);

  Counter #(.max('hffff), .width(16)) counter_1 (
    .up(1'b1), .clk(CLOCK), .Q(UP_COUNTER));  // open: clr, load, count, D, carry
  Counter #(.max('hffff), .width(16)) counter_2 (
    .up(1'b0), .clk(CLOCK), .Q(DOWN_COUNTER));  // open: clr, load, count, D, carry
endmodule

module Addition_Comparison (
  input  [15:0] Ri_IN,
  input  [15:0] Rj_IN,
  output [15:0] ADD_OUT,
  output [15:0] COMP_OUT
);

  wire [3:0] adder_1_cout;

  Adder #(.width(16)) adder_1 (.a(Ri_IN), .b(Rj_IN), .out(ADD_OUT), .cout(adder_1_cout[0]));  // open: cin
  Comparator #(.width(16)) comparator_1 (
    .a(Ri_IN), .b(Rj_IN), .gt(adder_1_cout[1]), .eq(adder_1_cout[2]), .lt(adder_1_cout[3]));
  assign COMP_OUT = {{12{1'b0}}, adder_1_cout};  // Bit_Extender bit_extender_1
endmodule

module ARITHMETIC_BLOCK (
  input  [15:0] Ri_IN,
  input  [15:0] Rj_IN,
  output [15:0] DIV_OUT,
  output [15:0] MUL_OUT,
  output [15:0] MUL_OVERFLOW,
  output [15:0] SUB_OUT,
  output [15:0] ADD_OUT,
  output [15:0] COMP_OUT
);

  wire [3:0] adder_1_cout;

  Divider #(.width(16)) divider_1 (.a(Ri_IN), .b(Rj_IN), .out(DIV_OUT));  // open: upper, rem
  Multiplier #(.width(16)) multiplier_1 (.a(Ri_IN), .b(Rj_IN), .out(MUL_OUT), .cout(MUL_OVERFLOW));  // open: cin
  Subtractor #(.width(16)) subtractor_1 (.a(Ri_IN), .b(Rj_IN), .out(SUB_OUT));  // open: bin, bout
  Adder #(.width(16)) adder_1 (.a(Ri_IN), .b(Rj_IN), .out(ADD_OUT), .cout(adder_1_cout[0]));  // open: cin
  Comparator #(.width(16)) comparator_1 (
    .a(Ri_IN), .b(Rj_IN), .gt(adder_1_cout[1]), .eq(adder_1_cout[2]), .lt(adder_1_cout[3]));
  assign COMP_OUT = {{12{1'b0}}, adder_1_cout};  // Bit_Extender bit_extender_1
endmodule

module LOGICAL_BLOCK (
  input  [15:0] Ri_LOGIC,
  input  [15:0] Rj_LOGIC,
  output [15:0] AND_OUT,
  output [15:0] OR_OUT
);

  and and_1 (AND_OUT[0], Ri_LOGIC[0], Rj_LOGIC[0]);
  and and_2 (AND_OUT[1], Ri_LOGIC[1], Rj_LOGIC[1]);
  and and_3 (AND_OUT[2], Ri_LOGIC[2], Rj_LOGIC[2]);
  and and_4 (AND_OUT[3], Ri_LOGIC[3], Rj_LOGIC[3]);
  and and_5 (AND_OUT[4], Ri_LOGIC[4], Rj_LOGIC[4]);
  and and_6 (AND_OUT[5], Ri_LOGIC[5], Rj_LOGIC[5]);
  and and_7 (AND_OUT[6], Ri_LOGIC[6], Rj_LOGIC[6]);
  and and_8 (AND_OUT[7], Ri_LOGIC[7], Rj_LOGIC[7]);
  and and_9 (AND_OUT[8], Ri_LOGIC[8], Rj_LOGIC[8]);
  and and_10 (AND_OUT[9], Ri_LOGIC[9], Rj_LOGIC[9]);
  and and_11 (AND_OUT[10], Ri_LOGIC[10], Rj_LOGIC[10]);
  and and_12 (AND_OUT[11], Ri_LOGIC[11], Rj_LOGIC[11]);
  and and_13 (AND_OUT[12], Ri_LOGIC[12], Rj_LOGIC[12]);
  and and_14 (AND_OUT[13], Ri_LOGIC[13], Rj_LOGIC[13]);
  and and_15 (AND_OUT[14], Ri_LOGIC[14], Rj_LOGIC[14]);
  and and_16 (AND_OUT[15], Ri_LOGIC[15], Rj_LOGIC[15]);
  or or_1 (OR_OUT[0], Ri_LOGIC[0], Rj_LOGIC[0]);
  or or_2 (OR_OUT[1], Ri_LOGIC[1], Rj_LOGIC[1]);
  or or_3 (OR_OUT[2], Ri_LOGIC[2], Rj_LOGIC[2]);
  or or_4 (OR_OUT[3], Ri_LOGIC[3], Rj_LOGIC[3]);
  or or_5 (OR_OUT[4], Ri_LOGIC[4], Rj_LOGIC[4]);
  or or_6 (OR_OUT[5], Ri_LOGIC[5], Rj_LOGIC[5]);
  or or_7 (OR_OUT[6], Ri_LOGIC[6], Rj_LOGIC[6]);
  or or_8 (OR_OUT[7], Ri_LOGIC[7], Rj_LOGIC[7]);
  or or_9 (OR_OUT[8], Ri_LOGIC[8], Rj_LOGIC[8]);
  or or_10 (OR_OUT[9], Ri_LOGIC[9], Rj_LOGIC[9]);
  or or_11 (OR_OUT[10], Ri_LOGIC[10], Rj_LOGIC[10]);
  or or_12 (OR_OUT[11], Ri_LOGIC[11], Rj_LOGIC[11]);
  or or_13 (OR_OUT[12], Ri_LOGIC[12], Rj_LOGIC[12]);
  or or_14 (OR_OUT[13], Ri_LOGIC[13], Rj_LOGIC[13]);
  or or_15 (OR_OUT[14], Ri_LOGIC[14], Rj_LOGIC[14]);
  or or_16 (OR_OUT[15], Ri_LOGIC[15], Rj_LOGIC[15]);
endmodule

module CORE (
  input  [15:0] UP_COUNTER,
  input  [15:0] DOWN_COUNTER,
  input  [15:0] Ri,
  input  [15:0] Rj,
  input  [7:0] OPCODE,
  output [15:0] OVERFLOW_OUT,
  output [15:0] DATA_OUT,
  output WRITE_ENABLE
);

  wire and_1_out, comparator_1_eq, multiplexer_3_out, not_1_out, or_1_out;
  wire [15:0] arithmetic_block_1_add_out, arithmetic_block_1_comp_out, arithmetic_block_1_div_out,
       arithmetic_block_1_mul_out, arithmetic_block_1_sub_out, logical_block_1_and_out,
       logical_block_1_or_out, multiplexer_1_out, multiplexer_2_out;

  Multiplexer #(.select(2), .width(16)) multiplexer_1 (
    .in0(Ri), .in1(Ri), .in2(Ri), .in3(UP_COUNTER), .out(multiplexer_1_out), .sel(OPCODE[1:0]));
  Multiplexer #(.select(2), .width(16)) multiplexer_2 (
    .in0(UP_COUNTER), .in1(DOWN_COUNTER), .in2(Rj), .in3(DOWN_COUNTER), .out(multiplexer_2_out),
    .sel(OPCODE[1:0]));
  Multiplexer #(.select(4)) multiplexer_3 (
    .in0(1'b1), .in1(1'b1), .in2(1'b1), .in3(1'b1), .in4(1'b1), .in8(1'b1), .in9(1'b1), .in12(1'b1),
    .out(multiplexer_3_out), .sel(OPCODE[5:2]));  // open: in5, in6, in7, in10, in11, in13, in14, in15
  or or_1 (or_1_out, OPCODE[6], OPCODE[7]);
  ARITHMETIC_BLOCK arithmetic_block_1 (
    .Ri_IN(multiplexer_1_out), .Rj_IN(multiplexer_2_out), .DIV_OUT(arithmetic_block_1_div_out),
    .MUL_OUT(arithmetic_block_1_mul_out), .MUL_OVERFLOW(OVERFLOW_OUT), .SUB_OUT(arithmetic_block_1_sub_out),
    .ADD_OUT(arithmetic_block_1_add_out), .COMP_OUT(arithmetic_block_1_comp_out));
  LOGICAL_BLOCK logical_block_1 (
    .Ri_LOGIC(multiplexer_1_out), .Rj_LOGIC(multiplexer_2_out), .AND_OUT(logical_block_1_and_out),
    .OR_OUT(logical_block_1_or_out));
  not not_1 (not_1_out, or_1_out);
  and and_1 (and_1_out, multiplexer_3_out, not_1_out);
  Multiplexer #(.select(4), .width(16)) multiplexer_4 (
    .in0(arithmetic_block_1_add_out), .in1(arithmetic_block_1_sub_out), .in2(arithmetic_block_1_mul_out),
    .in3(arithmetic_block_1_div_out), .in4(arithmetic_block_1_comp_out), .in8(logical_block_1_and_out),
    .in9(logical_block_1_or_out), .in12({16{1'b0}}), .in15({16{1'b0}}), .out(DATA_OUT), .sel(OPCODE[5:2]));  // open: in5, in6, in7, in10, in11, in13, in14
  Comparator comparator_1 (.a(OPCODE), .b(8'h41), .eq(comparator_1_eq));  // open: gt, lt
  or or_2 (WRITE_ENABLE, and_1_out, comparator_1_eq);
endmodule

module Vector_Unit (
  input  [7:0] OPCODE,
  input  [15:0] R0,
  input  [15:0] R1,
  input  [15:0] R2,
  input  [15:0] R3,
  input  [7:0] Vk,
  input  [7:0] Vj,
  input  [7:0] Vi,
  input  CLK,
  output [63:0] V0,
  output [63:0] V1,
  output [63:0] Vj_OUT,
  output [63:0] Vi_OUT
);

  wire bitselector_1_out, demultiplexer_1_out0, demultiplexer_1_out1, demultiplexer_1_out2,
       demultiplexer_1_out3, demultiplexer_1_out4, demultiplexer_1_out5, demultiplexer_1_out6,
       demultiplexer_1_out7;
  wire [2:0] bitselector_2_out, bitselector_3_out, bitselector_4_out;
  wire [63:0] demultiplexer_2_out0, demultiplexer_2_out1, demultiplexer_2_out2, demultiplexer_2_out3,
       demultiplexer_2_out4, demultiplexer_2_out5, demultiplexer_2_out6, demultiplexer_2_out7, register_3_q,
       register_4_q, register_5_q, register_6_q, register_7_q, register_8_q;

  BitSelector bitselector_1 (.in(OPCODE), .out(bitselector_1_out), .sel(3'b111));
  BitSelector #(.group(3)) bitselector_2 (.in(Vk), .out(bitselector_2_out), .sel(2'b00));
  Demultiplexer #(.select(3)) demultiplexer_1 (
    .out0(demultiplexer_1_out0), .out1(demultiplexer_1_out1), .out2(demultiplexer_1_out2),
    .out3(demultiplexer_1_out3), .out4(demultiplexer_1_out4), .out5(demultiplexer_1_out5),
    .out6(demultiplexer_1_out6), .out7(demultiplexer_1_out7), .in(bitselector_1_out), .sel(bitselector_2_out));
  Demultiplexer #(.select(3), .width(64)) demultiplexer_2 (
    .out0(demultiplexer_2_out0), .out1(demultiplexer_2_out1), .out2(demultiplexer_2_out2),
    .out3(demultiplexer_2_out3), .out4(demultiplexer_2_out4), .out5(demultiplexer_2_out5),
    .out6(demultiplexer_2_out6), .out7(demultiplexer_2_out7), .in({R3, R2, R1, R0}), .sel(bitselector_2_out));
  Register #(.trigger("falling"), .width(64)) register_1 (
    .D(demultiplexer_2_out0), .en(demultiplexer_1_out0), .clk(CLK), .Q(V0));  // open: clr
  Register #(.trigger("falling"), .width(64)) register_2 (
    .D(demultiplexer_2_out1), .en(demultiplexer_1_out1), .clk(CLK), .Q(V1));  // open: clr
  Register #(.trigger("falling"), .width(64)) register_3 (
    .D(demultiplexer_2_out2), .en(demultiplexer_1_out2), .clk(CLK), .Q(register_3_q));  // open: clr
  Register #(.trigger("falling"), .width(64)) register_4 (
    .D(demultiplexer_2_out3), .en(demultiplexer_1_out3), .clk(CLK), .Q(register_4_q));  // open: clr
  Register #(.trigger("falling"), .width(64)) register_5 (
    .D(demultiplexer_2_out4), .en(demultiplexer_1_out4), .clk(CLK), .Q(register_5_q));  // open: clr
  Register #(.trigger("falling"), .width(64)) register_6 (
    .D(demultiplexer_2_out5), .en(demultiplexer_1_out5), .clk(CLK), .Q(register_6_q));  // open: clr
  Register #(.trigger("falling"), .width(64)) register_7 (
    .D(demultiplexer_2_out6), .en(demultiplexer_1_out6), .clk(CLK), .Q(register_7_q));  // open: clr
  Register #(.trigger("falling"), .width(64)) register_8 (
    .D(demultiplexer_2_out7), .en(demultiplexer_1_out7), .clk(CLK), .Q(register_8_q));  // open: clr
  BitSelector #(.group(3)) bitselector_3 (.in(Vj), .out(bitselector_3_out), .sel(2'b00));
  Multiplexer #(.select(3), .width(64)) multiplexer_1 (
    .in0(V0), .in1(V1), .in2(register_3_q), .in3(register_4_q), .in4(register_5_q), .in5(register_6_q),
    .in6(register_7_q), .in7(register_8_q), .out(Vj_OUT), .sel(bitselector_3_out));
  BitSelector #(.group(3)) bitselector_4 (.in(Vi), .out(bitselector_4_out), .sel(2'b00));
  Multiplexer #(.select(3), .width(64)) multiplexer_2 (
    .in0(V0), .in1(V1), .in2(register_3_q), .in3(register_4_q), .in4(register_5_q), .in5(register_6_q),
    .in6(register_7_q), .in7(register_8_q), .out(Vi_OUT), .sel(bitselector_4_out));
endmodule

module Store_Check (
  input  ROM_0_CHECK,
  input  [7:0] OPCODE,
  input  ROM_1_CHECK,
  input  ROM_2_CHECK,
  input  ROM_3_CHECK,
  output MEM_0_WRITE,
  output MEM_1_WRITE,
  output MEM_2_WRITE,
  output MEM_3_WRITE
);

  wire comparator_1_eq, comparator_2_eq, comparator_3_eq, comparator_4_eq;

  and and_1 (MEM_0_WRITE, ROM_0_CHECK, comparator_1_eq);
  Comparator comparator_1 (.a(8'h41), .b(OPCODE), .eq(comparator_1_eq));  // open: gt, lt
  and and_2 (MEM_1_WRITE, ROM_1_CHECK, comparator_2_eq);
  Comparator comparator_2 (.a(8'h41), .b(OPCODE), .eq(comparator_2_eq));  // open: gt, lt
  and and_3 (MEM_2_WRITE, ROM_2_CHECK, comparator_3_eq);
  Comparator comparator_3 (.a(8'h41), .b(OPCODE), .eq(comparator_3_eq));  // open: gt, lt
  and and_4 (MEM_3_WRITE, ROM_3_CHECK, comparator_4_eq);
  Comparator comparator_4 (.a(8'h41), .b(OPCODE), .eq(comparator_4_eq));  // open: gt, lt
endmodule

module Vector_ALU (
  input  [63:0] Vi,
  input  [63:0] Vj,
  output [63:0] DOT_PROD
);

  wire [15:0] multiplier_1_out, multiplier_2_out, multiplier_3_out, multiplier_4_out, multiplier_5_out,
       multiplier_6_out, multiplier_7_out, multiplier_8_out;

  Multiplier #(.width(16)) multiplier_1 (.a(Vi[15:0]), .b(Vj[15:0]), .out(multiplier_1_out));  // open: cin, cout
  Multiplier #(.width(16)) multiplier_2 (.a(Vi[31:16]), .b(Vj[47:32]), .out(multiplier_2_out));  // open: cin, cout
  Multiplier #(.width(16)) multiplier_3 (.a(Vi[15:0]), .b(Vj[31:16]), .out(multiplier_3_out));  // open: cin, cout
  Multiplier #(.width(16)) multiplier_4 (.a(Vi[31:16]), .b(Vj[63:48]), .out(multiplier_4_out));  // open: cin, cout
  Multiplier #(.width(16)) multiplier_5 (.a(Vi[47:32]), .b(Vj[15:0]), .out(multiplier_5_out));  // open: cin, cout
  Multiplier #(.width(16)) multiplier_6 (.a(Vi[63:48]), .b(Vj[47:32]), .out(multiplier_6_out));  // open: cin, cout
  Multiplier #(.width(16)) multiplier_7 (.a(Vi[47:32]), .b(Vj[31:16]), .out(multiplier_7_out));  // open: cin, cout
  Multiplier #(.width(16)) multiplier_8 (.a(Vi[63:48]), .b(Vj[63:48]), .out(multiplier_8_out));  // open: cin, cout
  Adder #(.width(16)) adder_1 (.a(multiplier_1_out), .b(multiplier_2_out), .out(DOT_PROD[15:0]));  // open: cin, cout
  Adder #(.width(16)) adder_2 (.a(multiplier_3_out), .b(multiplier_4_out), .out(DOT_PROD[31:16]));  // open: cin, cout
  Adder #(.width(16)) adder_3 (.a(multiplier_5_out), .b(multiplier_6_out), .out(DOT_PROD[47:32]));  // open: cin, cout
  Adder #(.width(16)) adder_4 (.a(multiplier_7_out), .b(multiplier_8_out), .out(DOT_PROD[63:48]));  // open: cin, cout
endmodule
